# Fritzing sketch Plan (saved by Fritzing 0.9.0b)
breadboards: 1

parts:
  R1 = Rotary Potentiometer (Small) [maximum_resistance=100kΩ package=THT]
  J1 = Infrared Proximity Sensor
  Bauteil1 = Arduino Leonardo (Rev3b)
  LED1 = LED - 5mm [color="Red (633nm)" package="5 mm [THT]"]
  R2 = Resistor [tolerance=±5% resistance=220 package=THT]

nets:
  VCC: R1.leg1, J1.Vcc, Bauteil1.5V
  N1: R1.wiper, Bauteil1.A0
  GND: R1.leg2, J1.GND, Bauteil1.GND, LED1.cathode
  N2: J1.Vout, Bauteil1.A3
  N3: Bauteil1.D2/SDA, R2.Pin_0
  N4: LED1.anode, R2.Pin_1
